// Logisim project CPU_JUMP.circ as structural Verilog: 3 circuits, main circuit main
module main (
  input  in_1
);

  wire Clock;
  wire [7:0] cpu_1_screen;
  wire [31:0] mipsprogramrom_1_p1, mipsprogramrom_1_p2;

  Clock clock_1 (.out(Clock));
  LED led_1 (.in(Clock));
  // MIPSProgramROM mipsprogramrom_1: pin names not known; wires that end beside it: mipsprogramrom_1_p1, mipsprogramrom_1_p2, Clock
  CPU cpu_1 (
    .Reset(in_1), .Instruction(mipsprogramrom_1_p2), .Program_Counter(mipsprogramrom_1_p1),
    .Screen(cpu_1_screen));  // open: Keyboard, Kbd_Pull
  TTY tty_1 (.data(cpu_1_screen[6:0]), .clk(Clock), .we(cpu_1_screen[7]), .clr(in_1));

  // Other names for the same wires on the sheet: Reset = in_1
endmodule

module CPU (
  input  [7:0] Keyboard,
  input  Reset,
  input  [31:0] Instruction,
  output Kbd_Pull,
  output [7:0] Screen,
  output [31:0] Program_Counter
);

  wire ALU0, ALU1, and_1_out, ASrc, clock, JAL, JMP, JR, M2R, mips_alu_1_p4, MR, MW, Rdst, registerfile_1_p7,
       WE;
  wire [3:0] mips_alu_1_p3;
  wire [4:0] multiplexer_2_out, multiplexer_3_out;
  wire [8:8] Main_Control_p2;
  wire [31:0] adder_1_p3, adder_2_p3, bit_extender_1_out, datamemory_1_data_out, Main_Control_p3,
       mips_alu_1_p5, multiplexer_4_out, multiplexer_5_out, multiplexer_6_out, multiplexer_8_out, NEW_PC,
       registerfile_1_p8, shifter_1_out;

  Register #(.width(32)) PC (.D(NEW_PC), .Q(Program_Counter), .clk(clock), .clr(Reset));  // open: en
  Clock u_Clock (.out(clock));
  // Adder adder_1: pin names not known; wires that end beside it: 32'h4, Program_Counter, adder_1_p3
  // PLA Main_Control: pin names not known; wires that end beside it: Instruction[31:26], {JAL, JMP, Main_Control_p2[8], Rdst, WE, ASrc, MW, MR, M2R, ALU1, ALU0}, Main_Control_p3
  Multiplexer #(.width(32)) multiplexer_1 (
    .in0(multiplexer_8_out), .in1(adder_1_p3), .out(Main_Control_p3), .sel(JAL));  // open: en
  Multiplexer #(.width(5)) multiplexer_2 (
    .in0(Instruction[20:16]), .in1(Instruction[15:11]), .out(multiplexer_2_out), .sel(Rdst));  // open: en
  Multiplexer #(.width(5)) multiplexer_3 (
    .in0(multiplexer_2_out), .in1({5{1'b1}}), .out(multiplexer_3_out), .sel(JAL));  // open: en
  assign bit_extender_1_out = {{16{Instruction[15]}}, Instruction[15:0]};  // Bit_Extender bit_extender_1
  // RegisterFile registerfile_1: pin names not known; wires that end beside it: clock, WE, multiplexer_3_out, Instruction[25:21], Instruction[20:16], Reset, registerfile_1_p7, registerfile_1_p8
  Multiplexer #(.width(32)) multiplexer_4 (
    .in0(registerfile_1_p8), .in1(bit_extender_1_out), .out(multiplexer_4_out), .sel(ASrc));  // open: en
  Shifter #(.width(32)) shifter_1 (.in(bit_extender_1_out), .\dist (5'b00010), .out(shifter_1_out));
  // MIPS_ALU mips_alu_1: pin names not known; wires that end beside it: registerfile_1_p7, multiplexer_4_out, mips_alu_1_p3, mips_alu_1_p4, mips_alu_1_p5
  // PLA Control___ALU: pin names not known; wires that end beside it: {Instruction[5:0], ALU1, ALU0}, {JR, mips_alu_1_p3}
  and and_1 (and_1_out, Main_Control_p2[8], mips_alu_1_p4);
  Multiplexer #(.width(32)) multiplexer_5 (
    .in0(adder_1_p3), .in1(adder_2_p3), .out(multiplexer_5_out), .sel(and_1_out));  // open: en
  // Adder adder_2: pin names not known; wires that end beside it: adder_1_p3, shifter_1_out, adder_2_p3
  Multiplexer #(.width(32)) multiplexer_6 (
    .in0(multiplexer_5_out), .in1({adder_1_p3[31:28], Instruction[25:0], 2'b00}), .out(multiplexer_6_out),
    .sel(JMP));  // open: en
  Multiplexer #(.width(32)) multiplexer_7 (
    .in0(multiplexer_6_out), .in1(mips_alu_1_p5), .out(NEW_PC), .sel(JR));  // open: en
  DataMemory datamemory_1 (
    .Addr(mips_alu_1_p5), .Data(registerfile_1_p8), .Keyboard(Keyboard), .Data_Out(datamemory_1_data_out),
    .Screen(Screen), .Store(MW), .Load(MR), .Clock(clock), .Clear(Reset), .Kbd_Pull(Kbd_Pull));
  Multiplexer #(.width(32)) multiplexer_8 (
    .in0(mips_alu_1_p5), .in1(datamemory_1_data_out), .out(multiplexer_8_out), .sel(M2R));  // open: en

  // Other names for the same wires on the sheet: Op[31:0] = Instruction; kbd[7:0] = Keyboard;
  //   PC[31:0] = Program_Counter; scr[7:0] = Screen
endmodule

module DataMemory (
  input  [31:0] Addr,
  input  [31:0] Data,
  input  Clear,
  input  [7:0] Keyboard,
  input  Clock,
  input  Store,
  input  Load,
  output [31:0] Data_Out,
  output [7:0] Screen,
  output Kbd_Pull
);

  wire and_2_out, IO;
  wire [31:0] bit_extender_1_out, mips_ram_1_p7;

  or or_1 (IO, Addr[31], Addr[30], Addr[29], Addr[28], Addr[27], Addr[26], Addr[25], Addr[24], Addr[23], Addr[22], Addr[21], Addr[20]);
  and and_1 (Screen[7], IO, Store);
  and and_2 (and_2_out, Store, ~IO);  // AND_Gate
  // MIPS_RAM mips_ram_1: pin names not known; wires that end beside it: Addr[19:0], Data, and_2_out, Load, Clock, Clear, mips_ram_1_p7
  assign bit_extender_1_out = {{24{1'b0}}, Keyboard};  // Bit_Extender bit_extender_1
  and and_3 (Kbd_Pull, IO, Load, Clock);
  Multiplexer #(.width(32)) multiplexer_1 (
    .in0(mips_ram_1_p7), .in1(bit_extender_1_out), .out(Data_Out), .sel(IO));  // open: en

  assign Screen[6:0] = Data[6:0];

  // Other names for the same wires on the sheet: ctrl[11:0] = Addr[31:20]
endmodule
