// Logisim project CPU-PROJECT-1.circ as structural Verilog: 3 circuits, main circuit main
module main (
  input  in_1
);

  wire Clock, kbd_pull;
  wire [7:0] cpu_1_screen, kbd;
  wire [31:0] mipsprogramrom_1_p1, mipsprogramrom_1_p2;

  Clock clock_1 (.out(Clock));
  LED led_1 (.in(Clock));
  // MIPSProgramROM mipsprogramrom_1: pin names not known; wires that end beside it: mipsprogramrom_1_p1, mipsprogramrom_1_p2, Clock
  CPU cpu_1 (
    .Reset(in_1), .Instruction(mipsprogramrom_1_p2), .Program_Counter(mipsprogramrom_1_p1), .Keyboard(kbd),
    .Screen(cpu_1_screen), .Kbd_Pull(kbd_pull));
  TTY tty_1 (.data(cpu_1_screen[6:0]), .clk(Clock), .we(cpu_1_screen[7]), .clr(in_1));

  // Other names for the same wires on the sheet: Reset = in_1
endmodule

module CPU (
  input  [7:0] Keyboard,
  input  Reset,
  input  [31:0] Instruction,
  output Kbd_Pull,
  output [7:0] Screen,
  output [31:0] Program_Counter
);

  wire clock, mips_alu_1_p3, registerfile_1_p8;
  wire [4:0] multiplexer_1_out;
  wire [7:0] Control_Unit_p2;
  wire [31:0] adder_1_p3, bit_extender_1_out, datamemory_1_data_out, mips_alu_1_p2, mips_alu_1_p4,
       registerfile_1_p1, registerfile_1_p9;

  Register #(.width(32)) PC (.D(adder_1_p3), .Q(Program_Counter), .clk(clock), .clr(Reset));  // open: en
  Clock u_Clock (.out(clock));
  // Adder adder_1: pin names not known; wires that end beside it: 32'h4, Program_Counter, adder_1_p3
  // PLA Control_Unit: pin names not known; wires that end beside it: Instruction[31:26], Control_Unit_p2
  Multiplexer #(.width(5)) multiplexer_1 (
    .in0(Instruction[20:16]), .in1(Instruction[15:11]), .out(multiplexer_1_out), .sel(Control_Unit_p2[7]),
    .en(1'b1));
  assign bit_extender_1_out = {{16{Instruction[15]}}, Instruction[15:0]};  // Bit_Extender bit_extender_1
  // RegisterFile registerfile_1: pin names not known; wires that end beside it: registerfile_1_p1, clock, Control_Unit_p2[6], multiplexer_1_out, Instruction[25:21], Instruction[20:16], Reset, registerfile_1_p8, registerfile_1_p9
  // MIPS_ALU mips_alu_1: pin names not known; wires that end beside it: registerfile_1_p8, mips_alu_1_p2, mips_alu_1_p3, mips_alu_1_p4
  Multiplexer #(.width(32)) multiplexer_2 (
    .in0(registerfile_1_p9), .in1(bit_extender_1_out), .out(mips_alu_1_p2), .sel(Control_Unit_p2[5]),
    .en(1'b1));
  // PLA ALU_Control: pin names not known; wires that end beside it: {Instruction[5:0], Control_Unit_p2[1:0]}, mips_alu_1_p3
  DataMemory datamemory_1 (
    .Addr(mips_alu_1_p4), .Data(registerfile_1_p9), .Keyboard(Keyboard), .Data_Out(datamemory_1_data_out),
    .Screen(Screen), .Store(Control_Unit_p2[4]), .Load(Control_Unit_p2[3]), .Clock(clock), .Clear(Reset),
    .Kbd_Pull(Kbd_Pull));
  Multiplexer #(.width(32)) multiplexer_3 (
    .in0(mips_alu_1_p4), .in1(datamemory_1_data_out), .out(registerfile_1_p1), .sel(Control_Unit_p2[2]),
    .en(1'b1));

  // Other names for the same wires on the sheet: Op[31:0] = Instruction; kbd[7:0] = Keyboard;
  //   PC[31:0] = Program_Counter; scr[7:0] = Screen

  // Notes on the sheet:
  //   Increment PC by 4 at each tick  (this implements no jump or branch instructions)
endmodule

module DataMemory (
  input  [31:0] Addr,
  input  [31:0] Data,
  input  Clear,
  input  [7:0] Keyboard,
  input  Clock,
  input  Store,
  input  Load,
  output [31:0] Data_Out,
  output [7:0] Screen,
  output Kbd_Pull
);

  wire and_2_out, IO;
  wire [31:0] bit_extender_1_out, mips_ram_1_p7;

  or or_1 (IO, Addr[31], Addr[30], Addr[29], Addr[28], Addr[27], Addr[26], Addr[25], Addr[24], Addr[23], Addr[22], Addr[21], Addr[20]);
  and and_1 (Screen[7], IO, Store);
  and and_2 (and_2_out, Store, ~IO);  // AND_Gate
  // MIPS_RAM mips_ram_1: pin names not known; wires that end beside it: Addr[19:0], Data, and_2_out, Load, Clock, Clear, mips_ram_1_p7
  assign bit_extender_1_out = {{24{1'b0}}, Keyboard};  // Bit_Extender bit_extender_1
  and and_3 (Kbd_Pull, IO, Load, Clock);
  Multiplexer #(.width(32)) multiplexer_1 (
    .in0(mips_ram_1_p7), .in1(bit_extender_1_out), .out(Data_Out), .sel(IO), .en(1'b1));

  assign Screen[6:0] = Data[6:0];

  // Other names for the same wires on the sheet: ctrl[11:0] = Addr[31:20]
endmodule
