// Logisim project CPU-PROJECT (soln).circ as structural Verilog: 4 circuits, main circuit main
module main (
  input  in_1
);

  wire Clock;
  wire [7:0] cpu_1_screen;
  wire [31:0] mipsprogramrom_1_p1, mipsprogramrom_1_p2;

  Clock clock_1 (.out(Clock));
  LED led_1 (.in(Clock));
  // MIPSProgramROM mipsprogramrom_1: pin names not known; wires that end beside it: mipsprogramrom_1_p1, mipsprogramrom_1_p2
  CPU cpu_1 (
    .Clock(Clock), .Reset(in_1), .Instruction(mipsprogramrom_1_p2), .Program_Counter(mipsprogramrom_1_p1),
    .Screen(cpu_1_screen));  // open: Keyboard, Kbd_Pull
  TTY tty_1 (.data(cpu_1_screen[6:0]), .clk(Clock), .we(cpu_1_screen[7]), .clr(in_1));

  // Other names for the same wires on the sheet: Reset = in_1
endmodule

module CPU (
  input  Clock,
  input  [7:0] Keyboard,
  input  Reset,
  input  [31:0] Instruction,
  output Kbd_Pull,
  output [7:0] Screen,
  output [31:0] Program_Counter
);

  wire and_1_out, mips_alu_1_p4;
  wire [3:0] adder_1_p3;
  wire [4:0] multiplexer_2_out, multiplexer_3_out;
  wire [5:0] ALUControl_p2;
  wire [11:0] Control_p3;
  wire [27:0] adder_1_p3_2;
  wire [31:0] adder_2_p3, bit_extender_1_out_3, datamemory_1_data_out, mips_alu_1_p5, multiplexer_1_out,
       multiplexer_4_out, multiplexer_5_out, multiplexer_6_out, multiplexer_7_out, multiplexer_8_out,
       multiplexer_9_out, registerfile_1_p7, registerfile_1_p8;

  Register #(.width(32)) PC (.D(multiplexer_8_out), .Q(Program_Counter), .clk(Clock), .clr(Reset));  // open: en
  // Adder adder_1: pin names not known; wires that end beside it: 32'h4, Program_Counter, {adder_1_p3, adder_1_p3_2}
  Multiplexer #(.width(32), .enable("false")) multiplexer_1 (
    .in0(multiplexer_9_out), .in1({adder_1_p3, adder_1_p3_2}), .out(multiplexer_1_out), .sel(Control_p3[11]));
  Multiplexer #(.width(5), .enable("false")) multiplexer_2 (
    .in0(Instruction[20:16]), .in1(Instruction[15:11]), .out(multiplexer_2_out), .sel(Control_p3[0]));
  Multiplexer #(.width(5), .enable("false")) multiplexer_3 (
    .in0(multiplexer_2_out), .in1({5{1'b1}}), .out(multiplexer_3_out), .sel(Control_p3[11]));
  // PLA Control: pin names not known; wires that end beside it: Instruction[31:26], Clock, Control_p3
  // RegisterFile registerfile_1: pin names not known; wires that end beside it: multiplexer_1_out, Control_p3[1], multiplexer_3_out, Instruction[25:21], Instruction[20:16], Reset, registerfile_1_p7, registerfile_1_p8
  Bit_extender bit_extender_1 (.in_1(Instruction[15:0]), .out_3(bit_extender_1_out_3), .in_2(Control_p3[2]));
  Multiplexer #(.width(32), .enable("false")) multiplexer_4 (
    .in0({adder_1_p3, adder_1_p3_2}), .in1(registerfile_1_p7), .out(multiplexer_4_out), .sel(ALUControl_p2[5]));
  Multiplexer #(.width(32), .enable("false")) multiplexer_5 (
    .in0(registerfile_1_p7), .in1({{27{1'b0}}, Instruction[10:6]}), .out(multiplexer_5_out),
    .sel(ALUControl_p2[4]));
  Multiplexer #(.width(32), .enable("false")) multiplexer_6 (
    .in0(registerfile_1_p8), .in1(bit_extender_1_out_3), .out(multiplexer_6_out), .sel(Control_p3[6]));
  // PLA ALUControl: pin names not known; wires that end beside it: {Control_p3[5:3], Instruction[5:0]}, ALUControl_p2
  // Adder adder_2: pin names not known; wires that end beside it: multiplexer_4_out, {bit_extender_1_out_3[29:0], 2'b00}, adder_2_p3
  // MIPS_ALU mips_alu_1: pin names not known; wires that end beside it: multiplexer_5_out, multiplexer_6_out, ALUControl_p2[3:0], mips_alu_1_p4, mips_alu_1_p5
  Multiplexer #(.width(32), .enable("false")) multiplexer_7 (
    .in0(multiplexer_4_out), .in1(adder_2_p3), .out(multiplexer_7_out), .sel(and_1_out));
  and and_1 (and_1_out, mips_alu_1_p4, Control_p3[7]);
  Multiplexer #(.width(32), .enable("false")) multiplexer_8 (
    .in0(multiplexer_7_out), .in1({adder_1_p3, Instruction[25:0], 2'b00}), .out(multiplexer_8_out),
    .sel(Control_p3[10]));
  DataMemory datamemory_1 (
    .Addr(mips_alu_1_p5), .Data(registerfile_1_p8), .Keyboard(Keyboard), .Data_Out(datamemory_1_data_out),
    .Screen(Screen), .Store(Control_p3[8]), .Load(Control_p3[9]), .Clock(Clock), .Clear(Reset),
    .Kbd_Pull(Kbd_Pull));
  Multiplexer #(.width(32), .enable("false")) multiplexer_9 (
    .in0(mips_alu_1_p5), .in1(datamemory_1_data_out), .out(multiplexer_9_out), .sel(Control_p3[9]));

  // Other names for the same wires on the sheet: Op[31:0] = Instruction; kbd[7:0] = Keyboard;
  //   PC[31:0] = Program_Counter; scr[7:0] = Screen

  // Notes on the sheet:
  //   address
  //   rs
  //   rt
  //   rd
  //   immediate
  //   shamt
  //   funct
  //   opcode
  //   RegDst
  //   RegWrite
  //   JumpLink
  //   SignExt
  //   JumpR
  //   ALUOp
  //   Shamt
  //   ALUOp
  //   ALUSrc
  //   Branch
  //   Jump
  //   MemWrite
  //   MemRead
  //   MemRead
endmodule

module Bit_extender (
  input  [15:0] in_1,
  input  in_2,
  output [31:0] out_3
);

  wire [31:0] bit_extender_1_out, bit_extender_2_out;

  assign bit_extender_1_out = {{16{1'b0}}, in_1};  // Bit_Extender bit_extender_1
  assign bit_extender_2_out = {{16{in_1[15]}}, in_1};  // Bit_Extender bit_extender_2
  Multiplexer #(.width(32), .enable("false")) multiplexer_1 (
    .in0(bit_extender_1_out), .in1(bit_extender_2_out), .out(out_3), .sel(in_2));
endmodule

module DataMemory (
  input  [31:0] Addr,
  input  [31:0] Data,
  input  Clear,
  input  [7:0] Keyboard,
  input  Clock,
  input  Store,
  input  Load,
  output [31:0] Data_Out,
  output [7:0] Screen,
  output Kbd_Pull
);

  wire and_2_out, IO;
  wire [31:0] bit_extender_1_out, mips_ram_1_p7;

  or or_1 (IO, Addr[31], Addr[30], Addr[29], Addr[28], Addr[27], Addr[26], Addr[25], Addr[24], Addr[23], Addr[22], Addr[21], Addr[20]);
  and and_1 (Screen[7], IO, Store);
  and and_2 (and_2_out, Store, ~IO);  // AND_Gate
  // MIPS_RAM mips_ram_1: pin names not known; wires that end beside it: Addr[19:0], Data, and_2_out, Load, Clock, Clear, mips_ram_1_p7
  assign bit_extender_1_out = {{24{1'b0}}, Keyboard};  // Bit_Extender bit_extender_1
  and and_3 (Kbd_Pull, IO, Load, Clock);
  Multiplexer #(.width(32)) multiplexer_1 (
    .in0(mips_ram_1_p7), .in1(bit_extender_1_out), .out(Data_Out), .sel(IO));  // open: en

  assign Screen[6:0] = Data[6:0];

  // Other names for the same wires on the sheet: ctrl[11:0] = Addr[31:20]
endmodule
